# Fritzing sketch 4ch_relai (saved by Fritzing 0.9.6b)

parts:
  Mod1 = Raspberry Pi 4B
  U1 = 4-Channel 5v Relay Shield [package=relay-4ch5v10a]

nets:
  5V: Mod1.5V, U1.VCC
  GND: Mod1.GND, U1.GND
  N1: Mod1.GPIO17, U1.IN1
  N2: Mod1.GPIO18, U1.IN3
  N3: Mod1.GPIO27, U1.IN2
  N4: Mod1.GPIO22, U1.IN4

custom parts:
  4-Channel 5v Relay Shield: 4 Channel 5v Relay Shield w. 2x SPD-06VDC-SD-C
