# Fritzing sketch can_module (saved by Fritzing 0.9.6b)

parts:
  Mod1 = Raspberry Pi 4B
  M1 = Niren can bus module [package=THT]

nets:
  N1: Mod1.5V, M1.pin1
  N2: Mod1.GND, M1.pin2
  N3: Mod1.GPIO10, M1.pin5
  N4: Mod1.GPIO9, M1.pin4
  N5: Mod1.GPIO25, M1.pin7
  N6: Mod1.GPIO11, M1.pin6
  N7: Mod1.GPIO8, M1.pin3

notes:
  CAN high
  CAN low

custom parts:
  Niren can bus module: Niren can bus module availabe on ebay and others. No pcb view as no mechanical drawng and it wouldn't mount anyway.
